# Fritzing sketch wiring (saved by Fritzing 0.9.3b)

parts:
  Mod1 = Raspberry Pi 4B
  U1 = DRV8833
  Weeder_or_Water_Pump = DC Motor
  Cooling_Fan = Fan - Ventilador [package=THT]
  Left_Wheel_1 = DC Mini Metal Gear Motor
  Left_Wheel_2 = DC Mini Metal Gear Motor
  Right_Wheel_1 = DC Mini Metal Gear Motor
  Right_Wheel_2 = DC Mini Metal Gear Motor
  U2 = DRV8833

nets:
  VIN: Mod1.5V, U1.VIN, U2.VIN
  GND: Mod1.GND, U1.GND, U2.GND
  N1: Mod1.GPIO14, U1.BIN1
  N2: Mod1.GPIO15, U1.BIN2
  N3: Mod1.GPIO18, U1.AIN2
  N4: Mod1.GPIO23, U1.AIN1
  N5: Mod1.GPIO24, U2.BIN1
  N6: Mod1.GPIO25, U2.AIN1
  N7: U1.BOUT1, Right_Wheel_1.IN1, Right_Wheel_2.IN1
  N8: U1.BOUT2, Right_Wheel_1.IN2, Right_Wheel_2.IN2
  N9: U1.AOUT2, Left_Wheel_1.IN1, Left_Wheel_2.IN1
  N10: U1.AOUT1, Left_Wheel_1.IN2, Left_Wheel_2.IN2
  N11: Weeder_or_Water_Pump.pin_1, U2.AOUT2
  N12: Weeder_or_Water_Pump.pin_2, U2.AOUT1
  N13: Cooling_Fan.5V, U2.BOUT2
  N14: Cooling_Fan.GND, U2.BOUT1

custom parts:
  DRV8833: The DRV8833 provides a dual bridge motor driver solution for toys, printers, and other mechatronic applications.
  Fan - Ventilador: Ventilador de 2 pines, se encuentra comunmente en computadoras de escritorio
